// Logisim project 16_BITALU.circ as structural Verilog: 14 circuits, main circuit main
module main (
  input  [15:0] A,
  input  [15:0] B,
  input  [1:0] Comparision_Select,
  input  Carry_in,
  input  Shift_input,
  input  Overflow_select,
  input  [2:0] Operation_Select,
  output Overflow,
  output [15:0] Output
);

  wire Clear_out, Clk_out, Reset_out;

  Clock Clk (.out(Clk_out));
  Button Clear (.out(Clear_out));
  Button Reset (.out(Reset_out));
  ALU alu_1 (
    .A(A), .B(B), .Select(Comparision_Select), .Cin(Carry_in), .Shift_Input(Shift_input), .Clk(Clk_out),
    .Clear(Clear_out), .Reset(Reset_out), .Overflow_select(Overflow_select),
    .Operation_Select(Operation_Select), .Overflow(Overflow), .Output(Output));

  // Notes on the sheet:
  //   Comparision Select menu
  //   00- A<B
  //   01- A>B
  //   10- A=B
  //   11 - Don't care(x)
  //   Overflow Select menu
  //   0- Add overflow
  //   1- Subtract Overflow
  //   Operation Select menu
  //   000 - AND operation (Input: A,B)
  //   001 - OR operation (Input: A,B)
  //   010  - Add Operation (Input: A,B, Carry in,Overflow Select)
  //   011 - Subtract Operation (Input: A,B,Overflow Select)
  //   100 - Comparator Operation (Input: A,B,Comparision Select)
  //   101 - Left Shift Operation (Input: Shift Input,Clk,Clear)
  //   110 - Right Shift Operation (Input: Shift Input,Clk,Clear)
  //   111 - Reset (Input: Reset)
  //   If all bits are 1, The condition is true. Else, it is False
endmodule

// SUM
module Full_Adder (
  input  A,
  input  B,
  input  Cin,
  output SUM,
  output CARRY
);

  wire and_1_out, and_2_out, xor_1_out;

  xor xor_1 (xor_1_out, A, B);
  and and_1 (and_1_out, A, B);
  xor xor_2 (SUM, xor_1_out, Cin);
  and and_2 (and_2_out, xor_1_out, Cin);
  or or_1 (CARRY, and_2_out, and_1_out);
endmodule

module _4_bit_Adder (
  input  Cin,
  input  A0,
  input  A1,
  input  A2,
  input  A3,
  input  B0,
  input  B1,
  input  B2,
  input  B3,
  output S0,
  output S1,
  output S2,
  output Cprev,
  output S3,
  output Cout
);

  wire full_adder_1_carry, full_adder_2_carry;

  Full_Adder full_adder_1 (.A(A0), .B(B0), .Cin(Cin), .SUM(S0), .CARRY(full_adder_1_carry));
  Full_Adder full_adder_2 (.A(A1), .B(B1), .Cin(full_adder_1_carry), .SUM(S1), .CARRY(full_adder_2_carry));
  Full_Adder full_adder_3 (.A(A2), .B(B2), .Cin(full_adder_2_carry), .SUM(S2), .CARRY(Cprev));
  Full_Adder full_adder_4 (.A(A3), .B(B3), .Cin(Cprev), .SUM(S3), .CARRY(Cout));
endmodule

module Full_Subtractor (
  input  X,
  input  Y,
  input  Bin,
  output Diff,
  output Bout
);

  wire and_1_out, and_2_out, not_1_out, not_2_out, xor_1_out;

  not not_1 (not_1_out, X);
  xor xor_1 (xor_1_out, X, Y);
  and and_1 (and_1_out, not_1_out, Y);
  not not_2 (not_2_out, xor_1_out);
  and and_2 (and_2_out, not_2_out, Bin);
  xor xor_2 (Diff, xor_1_out, Bin);
  or or_1 (Bout, and_2_out, and_1_out);
endmodule

module Half_Subtractor (
  input  X,
  input  Y,
  output Diff,
  output Bout
);

  wire not_1_out;

  not not_1 (not_1_out, X);
  xor xor_1 (Diff, X, Y);
  and and_1 (Bout, not_1_out, Y);
endmodule

module _16_Bit_AND (
  input  [15:0] A,
  input  [15:0] B,
  output [15:0] Output
);

  assign Output = A & B;  // AND_Gate and_1, 16 bits wide
endmodule

module _16_Bit_OR (
  input  [15:0] A,
  input  [15:0] B,
  output [15:0] Output
);

  assign Output = A | B;  // OR_Gate or_1, 16 bits wide
endmodule

module _16_Bit_Adder (
  input  [15:0] B,
  input  [15:0] A,
  input  Cin,
  output out_4,
  output [15:0] Output
);

  wire n4_bit_adder_1_cout, n4_bit_adder_1_cprev, n4_bit_adder_2_cout, n4_bit_adder_3_cout,
       n4_bit_adder_4_cout;

  xor xor_1 (out_4, n4_bit_adder_1_cout, n4_bit_adder_1_cprev);
  _4_bit_Adder u_4_bit_adder_1 (
    .A0(A[12]), .A1(A[13]), .A2(A[14]), .A3(A[15]), .B0(B[12]), .B1(B[13]), .B2(B[14]), .B3(B[15]),
    .S0(Output[12]), .S1(Output[13]), .S2(Output[14]), .Cprev(n4_bit_adder_1_cprev), .S3(Output[15]),
    .Cin(n4_bit_adder_2_cout), .Cout(n4_bit_adder_1_cout));
  _4_bit_Adder u_4_bit_adder_2 (
    .A0(A[8]), .A1(A[9]), .A2(A[10]), .A3(A[11]), .B0(B[8]), .B1(B[9]), .B2(B[10]), .B3(B[11]),
    .S0(Output[8]), .S1(Output[9]), .S2(Output[10]), .S3(Output[11]), .Cin(n4_bit_adder_3_cout),
    .Cout(n4_bit_adder_2_cout));  // open: Cprev
  _4_bit_Adder u_4_bit_adder_3 (
    .A0(A[4]), .A1(A[5]), .A2(A[6]), .A3(A[7]), .B0(B[4]), .B1(B[5]), .B2(B[6]), .B3(B[7]), .S0(Output[4]),
    .S1(Output[5]), .S2(Output[6]), .S3(Output[7]), .Cin(n4_bit_adder_4_cout), .Cout(n4_bit_adder_3_cout));  // open: Cprev
  _4_bit_Adder u_4_bit_adder_4 (
    .A0(A[0]), .A1(A[1]), .A2(A[2]), .A3(A[3]), .B0(B[0]), .B1(B[1]), .B2(B[2]), .B3(B[3]), .S0(Output[0]),
    .S1(Output[1]), .S2(Output[2]), .S3(Output[3]), .Cin(Cin), .Cout(n4_bit_adder_4_cout));  // open: Cprev
endmodule

module _16_bit_subtractor (
  input  [15:0] B,
  input  [15:0] A,
  output Bout,
  output Overflow,
  output [15:0] Output
);

  wire full_subtractor_2_bout, full_subtractor_3_bout, full_subtractor_4_bout, full_subtractor_5_bout,
       full_subtractor_6_bout, full_subtractor_7_bout, full_subtractor_8_bout, full_subtractor_9_bout,
       full_subtractor_10_bout, full_subtractor_11_bout, full_subtractor_12_bout, full_subtractor_13_bout,
       full_subtractor_14_bout, full_subtractor_15_bout, half_subtractor_1_bout;

  Full_Subtractor full_subtractor_1 (
    .X(A[15]), .Y(B[15]), .Bin(full_subtractor_2_bout), .Diff(Output[15]), .Bout(Bout));
  xor xor_1 (Overflow, Bout, full_subtractor_2_bout);
  Full_Subtractor full_subtractor_2 (
    .X(A[14]), .Y(B[14]), .Bin(full_subtractor_3_bout), .Diff(Output[14]), .Bout(full_subtractor_2_bout));
  Full_Subtractor full_subtractor_3 (
    .X(A[13]), .Y(B[13]), .Bin(full_subtractor_4_bout), .Diff(Output[13]), .Bout(full_subtractor_3_bout));
  Full_Subtractor full_subtractor_4 (
    .X(A[12]), .Y(B[12]), .Bin(full_subtractor_5_bout), .Diff(Output[12]), .Bout(full_subtractor_4_bout));
  Full_Subtractor full_subtractor_5 (
    .X(A[11]), .Y(B[11]), .Bin(full_subtractor_6_bout), .Diff(Output[11]), .Bout(full_subtractor_5_bout));
  Full_Subtractor full_subtractor_6 (
    .X(A[10]), .Y(B[10]), .Bin(full_subtractor_7_bout), .Diff(Output[10]), .Bout(full_subtractor_6_bout));
  Full_Subtractor full_subtractor_7 (
    .X(A[9]), .Y(B[9]), .Bin(full_subtractor_8_bout), .Diff(Output[9]), .Bout(full_subtractor_7_bout));
  Full_Subtractor full_subtractor_8 (
    .X(A[8]), .Y(B[8]), .Bin(full_subtractor_9_bout), .Diff(Output[8]), .Bout(full_subtractor_8_bout));
  Full_Subtractor full_subtractor_9 (
    .X(A[7]), .Y(B[7]), .Bin(full_subtractor_10_bout), .Diff(Output[7]), .Bout(full_subtractor_9_bout));
  Full_Subtractor full_subtractor_10 (
    .X(A[6]), .Y(B[6]), .Bin(full_subtractor_11_bout), .Diff(Output[6]), .Bout(full_subtractor_10_bout));
  Full_Subtractor full_subtractor_11 (
    .X(A[5]), .Y(B[5]), .Bin(full_subtractor_12_bout), .Diff(Output[5]), .Bout(full_subtractor_11_bout));
  Full_Subtractor full_subtractor_12 (
    .X(A[4]), .Y(B[4]), .Bin(full_subtractor_14_bout), .Diff(Output[4]), .Bout(full_subtractor_12_bout));
  Full_Subtractor full_subtractor_13 (
    .X(A[2]), .Y(B[2]), .Bin(full_subtractor_15_bout), .Diff(Output[2]), .Bout(full_subtractor_13_bout));
  Full_Subtractor full_subtractor_14 (
    .X(A[3]), .Y(B[3]), .Bin(full_subtractor_13_bout), .Diff(Output[3]), .Bout(full_subtractor_14_bout));
  Full_Subtractor full_subtractor_15 (
    .X(A[1]), .Y(B[1]), .Bin(half_subtractor_1_bout), .Diff(Output[1]), .Bout(full_subtractor_15_bout));
  Half_Subtractor half_subtractor_1 (.X(A[0]), .Y(B[0]), .Diff(Output[0]), .Bout(half_subtractor_1_bout));
endmodule

module _16_Bit_Comparator (
  input  [15:0] B,
  input  [15:0] A,
  input  [1:0] S,
  output [15:0] Output
);

  wire and_1_out, Bout, nor_1_out, not_1_out, or_1_out;
  wire [15:0] n16_bit_subtractor_1_output;

  _16_bit_subtractor u_16_bit_subtractor_1 (
    .B(B), .A(A), .Output(n16_bit_subtractor_1_output), .Bout(Bout));  // open: Overflow
  and and_1 (and_1_out, Bout, or_1_out);
  or or_1 (or_1_out, n16_bit_subtractor_1_output[15], n16_bit_subtractor_1_output[14], n16_bit_subtractor_1_output[13], n16_bit_subtractor_1_output[12], n16_bit_subtractor_1_output[11], n16_bit_subtractor_1_output[10], n16_bit_subtractor_1_output[9], n16_bit_subtractor_1_output[8], n16_bit_subtractor_1_output[7], n16_bit_subtractor_1_output[6], n16_bit_subtractor_1_output[5], n16_bit_subtractor_1_output[4], n16_bit_subtractor_1_output[3], n16_bit_subtractor_1_output[2], n16_bit_subtractor_1_output[1], n16_bit_subtractor_1_output[0]);
  nor nor_1 (nor_1_out, and_1_out, not_1_out);
  Multiplexer #(.select(2), .enable("false")) multiplexer_1 (
    .in0(and_1_out), .in1(nor_1_out), .in2(not_1_out), .out(Output[15]), .sel(S));  // open: in3
  not not_1 (not_1_out, or_1_out);

  assign Output[14:0] = {15{Output[15]}};

  // Notes on the sheet:
  //   00- A<B
  //   01- A>B
  //   10- A=B
  //   11 - Don't care(x)
  //   If all bits are 1, The condition is true. Else, it is False
endmodule

module _16_Bit_Left_Shift (
  input  Clk,
  input  Input,
  input  Reset,
  output [15:0] Output
);

  wire d_ff_15_qn;

  D_Flip_Flop d_ff_1 (.clk(Clk), .D(Input), .Q(Output[0]), .reset(Reset));  // open: Qn, preset, en
  D_Flip_Flop d_ff_2 (.clk(Clk), .D(Output[0]), .Q(Output[1]), .reset(Reset));  // open: Qn, preset, en
  D_Flip_Flop d_ff_3 (.clk(Clk), .D(Output[1]), .Q(Output[2]), .reset(Reset));  // open: Qn, preset, en
  D_Flip_Flop d_ff_4 (.clk(Clk), .D(Output[2]), .Q(Output[3]), .reset(Reset));  // open: Qn, preset, en
  D_Flip_Flop d_ff_5 (.clk(Clk), .D(Output[3]), .Q(Output[4]), .reset(Reset));  // open: Qn, preset, en
  D_Flip_Flop d_ff_6 (.clk(Clk), .D(Output[4]), .Q(Output[5]), .reset(Reset));  // open: Qn, preset, en
  D_Flip_Flop d_ff_7 (.clk(Clk), .D(Output[5]), .Q(Output[6]), .reset(Reset));  // open: Qn, preset, en
  D_Flip_Flop d_ff_8 (.clk(Clk), .D(Output[6]), .Q(Output[7]), .reset(Reset));  // open: Qn, preset, en
  D_Flip_Flop d_ff_9 (.clk(Clk), .D(Output[7]), .Q(Output[8]), .reset(Reset));  // open: Qn, preset, en
  D_Flip_Flop d_ff_10 (.clk(Clk), .D(Output[8]), .Q(Output[9]), .reset(Reset));  // open: Qn, preset, en
  D_Flip_Flop d_ff_11 (.clk(Clk), .D(Output[9]), .Q(Output[10]), .reset(Reset));  // open: Qn, preset, en
  D_Flip_Flop d_ff_12 (.clk(Clk), .D(Output[10]), .Q(Output[11]), .reset(Reset));  // open: Qn, preset, en
  D_Flip_Flop d_ff_13 (.clk(Clk), .D(Output[11]), .Q(Output[12]), .reset(Reset));  // open: Qn, preset, en
  D_Flip_Flop d_ff_14 (.clk(Clk), .D(Output[12]), .Q(Output[13]), .reset(Reset));  // open: Qn, preset, en
  D_Flip_Flop d_ff_15 (.clk(Clk), .D(Output[13]), .Q(Output[14]), .Qn(d_ff_15_qn), .reset(Reset));  // open: preset, en
  D_Flip_Flop d_ff_16 (.clk(Clk), .D(Output[14]), .Q(Output[15]), .reset(Reset));  // open: Qn, preset, en
endmodule

module _16_Bit_Right_Shift (
  input  Clk,
  input  Input,
  input  Reset,
  output [15:0] Output
);

  wire d_ff_15_qn;

  D_Flip_Flop d_ff_1 (.clk(Clk), .D(Input), .Q(Output[15]), .reset(Reset));  // open: Qn, preset, en
  D_Flip_Flop d_ff_2 (.clk(Clk), .D(Output[15]), .Q(Output[14]), .reset(Reset));  // open: Qn, preset, en
  D_Flip_Flop d_ff_3 (.clk(Clk), .D(Output[14]), .Q(Output[13]), .reset(Reset));  // open: Qn, preset, en
  D_Flip_Flop d_ff_4 (.clk(Clk), .D(Output[13]), .Q(Output[12]), .reset(Reset));  // open: Qn, preset, en
  D_Flip_Flop d_ff_5 (.clk(Clk), .D(Output[12]), .Q(Output[11]), .reset(Reset));  // open: Qn, preset, en
  D_Flip_Flop d_ff_6 (.clk(Clk), .D(Output[11]), .Q(Output[10]), .reset(Reset));  // open: Qn, preset, en
  D_Flip_Flop d_ff_7 (.clk(Clk), .D(Output[10]), .Q(Output[9]), .reset(Reset));  // open: Qn, preset, en
  D_Flip_Flop d_ff_8 (.clk(Clk), .D(Output[9]), .Q(Output[8]), .reset(Reset));  // open: Qn, preset, en
  D_Flip_Flop d_ff_9 (.clk(Clk), .D(Output[8]), .Q(Output[7]), .reset(Reset));  // open: Qn, preset, en
  D_Flip_Flop d_ff_10 (.clk(Clk), .D(Output[7]), .Q(Output[6]), .reset(Reset));  // open: Qn, preset, en
  D_Flip_Flop d_ff_11 (.clk(Clk), .D(Output[6]), .Q(Output[5]), .reset(Reset));  // open: Qn, preset, en
  D_Flip_Flop d_ff_12 (.clk(Clk), .D(Output[5]), .Q(Output[4]), .reset(Reset));  // open: Qn, preset, en
  D_Flip_Flop d_ff_13 (.clk(Clk), .D(Output[4]), .Q(Output[3]), .reset(Reset));  // open: Qn, preset, en
  D_Flip_Flop d_ff_14 (.clk(Clk), .D(Output[3]), .Q(Output[2]), .reset(Reset));  // open: Qn, preset, en
  D_Flip_Flop d_ff_15 (.clk(Clk), .D(Output[2]), .Q(Output[1]), .Qn(d_ff_15_qn), .reset(Reset));  // open: preset, en
  D_Flip_Flop d_ff_16 (.clk(Clk), .D(Output[1]), .Q(Output[0]), .reset(Reset));  // open: Qn, preset, en
endmodule

module ALU (
  input  [15:0] A,
  input  Overflow_select,
  input  [15:0] B,
  input  [1:0] Select,
  input  Cin,
  input  Shift_Input,
  input  [2:0] Operation_Select,
  input  Clk,
  input  Clear,
  input  Reset,
  output Overflow,
  output [15:0] Output
);

  wire n16_bit_adder_1_out_4, n16_bit_subtractor_1_overflow;
  wire [15:0] n16_bit_adder_1_output, n16_bit_and_1_output, n16_bit_comparator_1_output,
       n16_bit_left_shift_1_output, n16_bit_or_1_output, n16_bit_right_shift_1_output,
       n16_bit_subtractor_1_output, reset_1_out_2;

  _16_Bit_Comparator u_16_bit_comparator_1 (.B(B), .A(A), .S(Select), .Output(n16_bit_comparator_1_output));
  _16_Bit_AND u_16_bit_and_1 (.A(A), .B(B), .Output(n16_bit_and_1_output));
  _16_Bit_OR u_16_bit_or_1 (.A(A), .B(B), .Output(n16_bit_or_1_output));
  _16_Bit_Adder u_16_bit_adder_1 (
    .B(B), .A(A), .Cin(Cin), .Output(n16_bit_adder_1_output), .out_4(n16_bit_adder_1_out_4));
  _16_bit_subtractor u_16_bit_subtractor_1 (
    .B(B), .A(A), .Output(n16_bit_subtractor_1_output), .Overflow(n16_bit_subtractor_1_overflow));  // open: Bout
  _16_Bit_Left_Shift u_16_bit_left_shift_1 (
    .Clk(Clk), .Input(Shift_Input), .Reset(Clear), .Output(n16_bit_left_shift_1_output));
  _16_Bit_Right_Shift u_16_bit_right_shift_1 (
    .Clk(Clk), .Input(Shift_Input), .Reset(Clear), .Output(n16_bit_right_shift_1_output));
  Reset reset_1 (.in_1(Reset), .out_2(reset_1_out_2));
  Multiplexer #(.enable("false")) multiplexer_1 (
    .in0(n16_bit_adder_1_out_4), .in1(n16_bit_subtractor_1_overflow), .out(Overflow), .sel(Overflow_select));
  Multiplexer #(.select(3), .width(16), .enable("false")) multiplexer_2 (
    .in0(n16_bit_and_1_output), .in1(n16_bit_or_1_output), .in2(n16_bit_adder_1_output),
    .in3(n16_bit_subtractor_1_output), .in4(n16_bit_comparator_1_output), .in5(n16_bit_left_shift_1_output),
    .in6(n16_bit_right_shift_1_output), .in7(reset_1_out_2), .out(Output), .sel(Operation_Select));
endmodule

module Reset (
  input  in_1,
  output [15:0] out_2
);


  assign out_2 = {16{in_1}};
endmodule
